# Fritzing sketch blink_a_led (saved by Fritzing 0.3.16b)
breadboards: 1

parts:
  Composants1 = Jaluino Medium
  R1 = Resistor [resistance=1k package=THT]
  LED1 = Red LED - 5mm

nets:
  N1: Composants1.conGND2, LED1.anode
  N2: Composants1.conRA0, R1.Pin_1
  N3: R1.Pin_0, LED1.cathode
