# Fritzing sketch crumboard_blink_leds (saved by Fritzing 0.3.16b)

parts:
  Composants1 = Crumboard shield
  Composants2 = Jumper
  Composants3 = Jumper

nets:
  N1: Composants1.con5V, Composants1.pin3W, Composants1.pin4W, Composants1.pin5W, Composants1.pin6W, Composants1.pin7W, Composants1.pin9W, Composants1.pin10W, Composants1.pin11W, Composants1.pin12W, Composants1.pin13W, Composants1.pin15W, Composants1.pin16W, Composants1.pin17W, Composants1.pin18W, Composants1.pin19W, Composants1.pin21W, Composants1.pin22W, Composants1.pin23W, Composants1.pin24W, Composants1.pin25W
  N2: Composants1.conGND2, Composants1.pin3X, Composants1.pin4X, Composants1.pin5X, Composants1.pin6X, Composants1.pin7X, Composants1.pin9X, Composants1.pin10X, Composants1.pin11X, Composants1.pin12X, Composants1.pin13X, Composants1.pin15X, Composants1.pin16X, Composants1.pin17X, Composants1.pin18X, Composants1.pin19X, Composants1.pin21X, Composants1.pin22X, Composants1.pin23X, Composants1.pin24X, Composants1.pin25X
  N3: Composants1.conJP11, Composants2.conJ1
  N4: Composants1.conJP12, Composants2.conJ2
  N5: Composants1.conJP21, Composants3.conJ1
  N6: Composants1.conJP22, Composants3.conJ2

notes:
  Put a jumper on JP1 to enable LED on RA0, and JP2 to enable LED on RC2
